# Fritzing sketch BLekeyboard (saved by Fritzing 0.8.7b)
breadboards: 1

parts:
  U2 = ESP32-38PinWide [part_number=ESP32-38PinWide]
  J2 = female pin header, 2 pins [form="♀ (female)"]
  J3 = female pin header, 2 pins [form="♀ (female)"]
  J4 = female pin header, 2 pins [form="♀ (female)"]
  J5 = female pin header, 2 pins [form="♀ (female)"]
  J6 = female pin header, 2 pins [form="♀ (female)"]
  J7 = female pin header, 2 pins [form="♀ (female)"]
  J8 = female pin header, 2 pins [form="♀ (female)"]
  J1 = female pin header, 2 pins [form="♀ (female)"]

nets:
  N1: U2.GND, J1.pin2
  N2: U2.GPIO0, J1.pin1
  N3: U2.GPIO4, J2.pin1
  N4: U2.GPIO16, J3.pin1
  N5: U2.GPIO17, J4.pin1
  N6: U2.GPIO5, J5.pin1
  N7: U2.GPIO18, J6.pin1
  N8: U2.GPIO19, J7.pin1
  N9: U2.GPIO21, J8.pin1

custom parts:
  ESP32-38PinWide: Generic 38-Pin ESP32 with wide format (only access to one side of pins on a breadboard) based on Stephen Lilley's HiLetgo ESP-WROOM-32 ESP32 ESP-32S Development Board.
